# Fritzing sketch xiao-ble-wiring (saved by Fritzing 1.0.2b)

parts:
  A2 = XIAO NRF52840 sense SMD
  Mod2 = OLED Mono 0.56 inch blue or white
  S2 = Momentary Switch [package=ksa_sealed_tac_switch]
  U1 = SWITCH_SPDT [package=kps-1290]
  A3 = XIAO NRF52840 sense SMD
  Mod3 = OLED Mono 0.56 inch blue or white
  S3 = Momentary Switch [package=ksa_sealed_tac_switch]
  U2 = LIPO-110mAh [package=lipo-110]  # not connected

nets:
  N1: A2.Pin_2, A2.Pin_13, A2.Pin_21, Mod2.GND
  N2: A2.Pin_7, S2.1
  N3: A2.Pin_9, Mod2.SDA
  N4: A2.Pin_10, Mod2.SCL
  N5: A2.Pin_20, Mod2.VCC
  N6: U1.P, A3.Pin_12
  N7: A3.Pin_2, A3.Pin_13, A3.Pin_21, Mod3.GND
  N8: A3.Pin_7, S3.3
  N9: A3.Pin_9, Mod3.SDA
  N10: A3.Pin_10, Mod3.SCL
  N11: A3.Pin_20, Mod3.VCC

notes:
  5v power source
  Screen power 3.3v

custom parts:
  XIAO NRF52840 sense SMD: The Seeed Studio XIAO family, Seeed Studio XIAO nRF52840 is equipped with a powerful Nordic nRF52840 MCU which integrates Bluetooth 5.0 connectivity. This is the SMD version there is also a THT version of the part.
  OLED Mono 0.56 inch blue or white: OLED, I2C 3.3V - 5V Blue and White text versions
